// Logisim project 6502.circ as structural Verilog: 5 circuits, main circuit main
module main (
);

  wire A_LOAD, ACC_LOAD, adder_2_cout, ADDR_A_HI_LOAD, ADDR_A_LO_LOAD, ADDR_B_HI_LOAD, ADDR_B_LO_LOAD,
       ADDRESS_B, ADDRESS_OFFSET_CI, ADDRESS_OFFSET_LOAD, ALU_CARRY, ALU_NEGATIVE, ALU_ZERO, and_1_out,
       and_2_out, and_3_out, and_4_out, and_5_out, and_6_out, and_7_out, asl_1_carry, B_LOAD, B_SEQ_RESET,
       brol_1_carry, bror_1_carry, CARRY_FLAG, CLK, COUNT_ADDRESS, counter_1_carry, counter_2_carry,
       DECIMAL_FLAG, decoder_1_out0, decoder_1_out1, decoder_1_out2, decoder_1_out3, decoder_1_out4,
       decoder_1_out5, decoder_1_out6, decoder_1_out7, decoder_1_out8, decoder_1_out9, decoder_1_out10,
       decoder_1_out11, decoder_1_out12, decoder_1_out13, decoder_1_out14, decoder_1_out15, decoder_2_out15,
       decoder_3_out1, decoder_3_out2, decoder_3_out3, decoder_3_out4, decoder_3_out5, decoder_3_out6,
       decoder_3_out7, decoder_3_out8, decoder_3_out9, decoder_3_out10, decoder_3_out11, decoder_3_out12,
       decoder_3_out13, decoder_3_out14, decoder_3_out15, decoder_4_out1, decoder_4_out2, decoder_4_out3,
       decoder_4_out4, decoder_4_out5, decoder_4_out6, decoder_5_out1, decoder_5_out2, decoder_5_out3,
       decoder_5_out4, decoder_5_out5, decoder_5_out6, decoder_5_out7, decoder_5_out8, decoder_5_out9,
       decoder_5_out10, decoder_5_out11, decoder_5_out12, FLAG_FALSE, INTERRUPT_DISABLE_FLAG, IR_LOAD,
       lsr_1_carry, NEGATIVE_FLAG, not_1_out, not_2_out, not_3_out, not_4_out, not_5_out, not_6_out,
       not_7_out, not_8_out, or_1_out, or_2_out, or_5_out, or_6_out, or_7_out, or_8_out, or_9_out, or_10_out,
       or_11_out, or_12_out, or_13_out, or_14_out, or_15_out, or_16_out, OVERFLOW_FLAG, PC_HI_LOAD,
       PC_LO_LOAD, RESET, SP_LOAD, subtractor_1_bout, X_LOAD, Y_LOAD, ZERO_FLAG;
  wire [1:0] CONSTV;
  wire [2:0] FLAG_CMD;
  wire [3:0] ALU_OP, counter_1_q;
  wire [7:0] A_STORE, ACC_STORE, adder_2_out, ADDRESS_OFFSET_q, ADR_AH_STORE, ADR_AL_STORE, ADR_BH_STORE,
       ADR_BL_STORE, ALU_OUT, and_8_out, asl_1_q, B_STORE, brol_1_q, bror_1_q, CONST_STORE, DBUS,
       INSTRUCTION_REGISTER_q, lsr_1_q, or_4_out, PC_HI_STORE, PC_LO_STORE, ram_1_dout, SP_STORE,
       subtractor_1_out, X_STORE, xor_1_out, Y_STORE;
  wire [15:0] adder_1_out, multiplexer_1_out;
  wire [30:0] MICROCODE_STEP;

  Register EFF_ADDRESS_B_HIGH (.D(DBUS), .en(ADDR_B_HI_LOAD), .clk(CLK), .Q(ADR_BH_STORE), .clr(RESET));
  Register EFF_ADDRESS_B_LOW (.D(DBUS), .en(ADDR_B_LO_LOAD), .clk(CLK), .Q(ADR_BL_STORE), .clr(RESET));
  and and_1 (and_1_out, CLK, MICROCODE_STEP[22]);
  Register INDEX_X (.D(DBUS), .en(X_LOAD), .clk(CLK), .Q(X_STORE), .clr(RESET));
  Register INDEX_Y (.D(DBUS), .en(Y_LOAD), .clk(CLK), .Q(Y_STORE), .clr(RESET));
  Counter STACK_POINTER (
    .load(SP_LOAD), .D(DBUS), .count(MICROCODE_STEP[26]), .Q(SP_STORE), .up(MICROCODE_STEP[25]), .clk(CLK),
    .clr(RESET));  // open: carry
  Register EFF_ADDRESS_A_HIGH (.D(DBUS), .en(ADDR_A_HI_LOAD), .clk(CLK), .Q(ADR_AH_STORE), .clr(RESET));
  Register EFF_ADDRESS_A_LOW (.D(DBUS), .en(ADDR_A_LO_LOAD), .clk(CLK), .Q(ADR_AL_STORE), .clr(RESET));
  Register ADDRESS_OFFSET (.D(DBUS), .en(ADDRESS_OFFSET_LOAD), .clk(CLK), .Q(ADDRESS_OFFSET_q), .clr(or_1_out));
  or or_1 (or_1_out, and_1_out, RESET);
  Register ACCUMULATOR (.D(DBUS), .en(ACC_LOAD), .clk(CLK), .Q(ACC_STORE), .clr(RESET));
  Clock clock_1 (.out(CLK));
  Button button_1 (.out(RESET));
  Multiplexer #(.width(16)) multiplexer_1 (
    .in0({ADR_AH_STORE, ADR_AL_STORE}), .in1({ADR_BH_STORE, ADR_BL_STORE}), .out(multiplexer_1_out),
    .sel(ADDRESS_B));
  Adder #(.width(16)) adder_1 (
    .a(multiplexer_1_out), .b({{8{1'b0}}, ADDRESS_OFFSET_q}), .out(adder_1_out), .cin(ADDRESS_OFFSET_CI));  // open: cout
  LED led_1 (.in(decoder_2_out15));
  or or_2 (or_2_out, B_SEQ_RESET, FLAG_FALSE, RESET, counter_1_carry);
  RAM #(.addrWidth(16), .readbehav("war"), .trigger("falling")) ram_1 (
    .addr(adder_1_out), .we(decoder_2_out15), .oe(1'b1), .clk(CLK), .din(DBUS), .dout(ram_1_dout));
  LedBar #(.matrixcols(16)) ledbar_1 (
    .led0(decoder_1_out0), .led1(decoder_1_out1), .led2(decoder_1_out2), .led3(decoder_1_out3),
    .led4(decoder_1_out4), .led5(decoder_1_out5), .led6(decoder_1_out6), .led7(decoder_1_out7),
    .led8(decoder_1_out8), .led9(decoder_1_out9), .led10(decoder_1_out10), .led11(decoder_1_out11),
    .led12(decoder_1_out12), .led13(decoder_1_out13), .led14(decoder_1_out14), .led15(decoder_1_out15));
  Decoder #(.enable("false"), .select(4)) decoder_1 (
    .out0(decoder_1_out0), .out1(decoder_1_out1), .out2(decoder_1_out2), .out3(decoder_1_out3),
    .out4(decoder_1_out4), .out5(decoder_1_out5), .out6(decoder_1_out6), .out7(decoder_1_out7),
    .out8(decoder_1_out8), .out9(decoder_1_out9), .out10(decoder_1_out10), .out11(decoder_1_out11),
    .out12(decoder_1_out12), .out13(decoder_1_out13), .out14(decoder_1_out14), .out15(decoder_1_out15),
    .sel(counter_1_q));
  Counter #(.max('hf), .width(4)) counter_1 (
    .load(1'b0), .count(1'b1), .Q(counter_1_q), .carry(counter_1_carry), .up(1'b1), .clk(CLK), .clr(or_2_out));  // open: D
  LED led_2 (.in(X_LOAD));
  LED led_3 (.in(Y_LOAD));
  LED led_4 (.in(SP_LOAD));
  LED led_5 (.in(ADDR_A_HI_LOAD));
  LED led_6 (.in(ADDR_A_LO_LOAD));
  LED led_7 (.in(ADDR_B_HI_LOAD));
  LED led_8 (.in(ADDR_B_LO_LOAD));
  LED led_9 (.in(ACC_LOAD));
  LED led_10 (.in(A_LOAD));
  LED led_11 (.in(B_LOAD));
  LED led_12 (.in(IR_LOAD));
  LED led_13 (.in(PC_HI_LOAD));
  LED led_14 (.in(PC_LO_LOAD));
  LED led_15 (.in(ADDRESS_OFFSET_LOAD));
  Register INSTRUCTION_REGISTER (.D(DBUS), .en(IR_LOAD), .clk(CLK), .Q(INSTRUCTION_REGISTER_q), .clr(RESET));
  Counter counter_2 (
    .load(PC_LO_LOAD), .D(DBUS), .count(COUNT_ADDRESS), .Q(PC_LO_STORE), .carry(counter_2_carry), .up(1'b1),
    .clk(CLK), .clr(RESET));
  LED led_16 (.in(decoder_3_out15));
  ROM #(.addrWidth(12), .dataWidth(31)) rom_1 (
    .addr({INSTRUCTION_REGISTER_q, counter_1_q}),
    .data({MICROCODE_STEP[30:25], ADDRESS_OFFSET_CI, ADDRESS_B, MICROCODE_STEP[22:21], B_SEQ_RESET, COUNT_ADDRESS, MICROCODE_STEP[18:17], CONSTV, FLAG_CMD, ALU_OP, MICROCODE_STEP[7:0]}));
  Counter counter_3 (
    .load(PC_HI_LOAD), .D(DBUS), .count(counter_2_carry), .Q(PC_HI_STORE), .up(1'b1), .clk(CLK), .clr(RESET));  // open: carry
  Decoder #(.enable("false"), .select(4)) decoder_2 (
    .out1(X_LOAD), .out2(Y_LOAD), .out3(SP_LOAD), .out4(ADDR_A_HI_LOAD), .out5(ADDR_A_LO_LOAD),
    .out6(ADDR_B_HI_LOAD), .out7(ADDR_B_LO_LOAD), .out8(ACC_LOAD), .out9(A_LOAD), .out10(B_LOAD),
    .out11(IR_LOAD), .out12(PC_HI_LOAD), .out13(PC_LO_LOAD), .out14(ADDRESS_OFFSET_LOAD),
    .out15(decoder_2_out15), .sel(MICROCODE_STEP[7:4]));  // open: out0
  Decoder #(.enable("false"), .select(4)) decoder_3 (
    .out1(decoder_3_out1), .out2(decoder_3_out2), .out3(decoder_3_out3), .out4(decoder_3_out4),
    .out5(decoder_3_out5), .out6(decoder_3_out6), .out7(decoder_3_out7), .out8(decoder_3_out8),
    .out9(decoder_3_out9), .out10(decoder_3_out10), .out11(decoder_3_out11), .out12(decoder_3_out12),
    .out13(decoder_3_out13), .out14(decoder_3_out14), .out15(decoder_3_out15), .sel(MICROCODE_STEP[3:0]));  // open: out0
  LED led_17 (.in(decoder_3_out1));
  LED led_18 (.in(decoder_3_out2));
  LED led_19 (.in(decoder_3_out3));
  LED led_20 (.in(decoder_3_out4));
  LED led_21 (.in(decoder_3_out5));
  LED led_22 (.in(decoder_3_out6));
  LED led_23 (.in(decoder_3_out7));
  LED led_24 (.in(decoder_3_out8));
  LED led_25 (.in(decoder_3_out9));
  LED led_26 (.in(decoder_3_out10));
  LED led_27 (.in(decoder_3_out11));
  LED led_28 (.in(decoder_3_out12));
  LED led_29 (.in(decoder_3_out13));
  LED led_30 (.in(decoder_3_out14));
  Multiplexer #(.select(4), .width(8)) multiplexer_2 (
    .in1(X_STORE), .in2(Y_STORE), .in3(SP_STORE), .in4(ADR_AH_STORE), .in5(ADR_AL_STORE), .in6(ADR_BH_STORE),
    .in7(ADR_BL_STORE), .in8(ACC_STORE), .in9(A_STORE), .in10(B_STORE), .in11(CONST_STORE),
    .in12(PC_HI_STORE), .in13(PC_LO_STORE), .in14(ALU_OUT), .in15(ram_1_dout), .out(DBUS),
    .sel(MICROCODE_STEP[3:0]));  // open: in0
  Decoder #(.enable("false"), .select(3)) decoder_4 (
    .out1(decoder_4_out1), .out2(decoder_4_out2), .out3(decoder_4_out3), .out4(decoder_4_out4),
    .out5(decoder_4_out5), .out6(decoder_4_out6), .sel(FLAG_CMD));  // open: out0, out7
  Multiplexer #(.select(2), .width(8)) multiplexer_3 (
    .in0({8{1'b0}}), .in1(8'h1), .in2({8{1'b1}}), .out(CONST_STORE), .sel(CONSTV));  // open: in3
  or or_3 (FLAG_FALSE, and_4_out, and_3_out, and_2_out, and_5_out, and_6_out, and_7_out);
  and and_2 (and_2_out, decoder_4_out1, CARRY_FLAG);
  and and_3 (and_3_out, decoder_4_out5, NEGATIVE_FLAG);
  and and_4 (and_4_out, ~NEGATIVE_FLAG, decoder_4_out6);  // AND_Gate
  Register A_REGISTER (.D(DBUS), .en(A_LOAD), .clk(CLK), .Q(A_STORE), .clr(RESET));
  Register B_REGISTER (.D(DBUS), .en(B_LOAD), .clk(CLK), .Q(B_STORE), .clr(RESET));
  and and_5 (and_5_out, decoder_4_out2, ~CARRY_FLAG);  // AND_Gate
  and and_6 (and_6_out, decoder_4_out3, ZERO_FLAG);
  and and_7 (and_7_out, decoder_4_out4, ~ZERO_FLAG);  // AND_Gate
  Decoder #(.enable("false"), .select(4)) decoder_5 (
    .out1(decoder_5_out1), .out2(decoder_5_out2), .out3(decoder_5_out3), .out4(decoder_5_out4),
    .out5(decoder_5_out5), .out6(decoder_5_out6), .out7(decoder_5_out7), .out8(decoder_5_out8),
    .out9(decoder_5_out9), .out10(decoder_5_out10), .out11(decoder_5_out11), .out12(decoder_5_out12),
    .sel(MICROCODE_STEP[30:27]));  // open: out0, out13, out14, out15
  assign and_8_out = A_STORE & B_STORE;  // AND_Gate and_8, 8 bits wide
  assign or_4_out = A_STORE | B_STORE;  // OR_Gate or_4, 8 bits wide
  assign xor_1_out = A_STORE ^ B_STORE;  // XOR_Gate xor_1, 8 bits wide
  Adder adder_2 (.a(A_STORE), .b(B_STORE), .out(adder_2_out), .cin(CARRY_FLAG), .cout(adder_2_cout));
  Subtractor subtractor_1 (
    .a(A_STORE), .b(B_STORE), .out(subtractor_1_out), .bin(CARRY_FLAG), .bout(subtractor_1_bout));
  ASL asl_1 (.D(A_STORE), .Q(asl_1_q), .CARRY(asl_1_carry));
  LSR lsr_1 (.D(A_STORE), .Q(lsr_1_q), .CARRY(lsr_1_carry));
  bROL brol_1 (.D(A_STORE), .CIN(CARRY_FLAG), .Q(brol_1_q), .CARRY(brol_1_carry));
  bROR bror_1 (.CIN(CARRY_FLAG), .D(A_STORE), .Q(bror_1_q), .CARRY(bror_1_carry));
  or or_5 (or_5_out, MICROCODE_STEP[17], decoder_5_out2);
  Multiplexer #(.select(4), .width(8)) multiplexer_4 (
    .in0(and_8_out), .in1(or_4_out), .in2(xor_1_out), .in3(adder_2_out), .in4(subtractor_1_out),
    .in5(asl_1_q), .in6(lsr_1_q), .in7(brol_1_q), .in8(bror_1_q), .out(ALU_OUT), .sel(ALU_OP));  // open: in9, in10, in11, in12, in13, in14, in15
  Multiplexer #(.select(4)) multiplexer_5 (
    .in0(1'b0), .in1(1'b0), .in2(1'b0), .in3(adder_2_cout), .in4(1'b0), .in5(asl_1_carry), .in6(lsr_1_carry),
    .in7(brol_1_carry), .in8(bror_1_carry), .in9(1'b0), .in10(1'b0), .in11(1'b0), .in12(1'b0), .in13(1'b0),
    .in14(1'b0), .in15(1'b0), .out(ALU_CARRY), .sel(ALU_OP));
  or or_6 (or_6_out, ALU_ZERO, decoder_5_out4);
  or or_7 (or_7_out, MICROCODE_STEP[18], decoder_5_out4);
  or or_8 (or_8_out, ALU_CARRY, decoder_5_out2);
  not not_1 (not_1_out, ALU_OUT[0]);
  not not_2 (not_2_out, ALU_OUT[1]);
  not not_3 (not_3_out, ALU_OUT[2]);
  not not_4 (not_4_out, ALU_OUT[3]);
  and and_9 (ALU_ZERO, not_1_out, not_2_out, not_3_out, not_4_out, not_5_out, not_6_out, not_7_out, not_8_out);
  not not_5 (not_5_out, ALU_OUT[4]);
  not not_6 (not_6_out, ALU_OUT[5]);
  not not_7 (not_7_out, ALU_OUT[6]);
  not not_8 (not_8_out, ALU_OUT[7]);
  Multiplexer #(.select(4)) multiplexer_6 (
    .in0(1'b0), .in1(1'b0), .in2(1'b0), .in3(1'b0), .in4(subtractor_1_bout), .in5(1'b0), .in6(1'b0),
    .in7(1'b0), .in8(1'b0), .in9(1'b0), .in10(1'b0), .in11(1'b0), .in12(1'b0), .in13(1'b0), .in14(1'b0),
    .in15(1'b0), .out(ALU_NEGATIVE), .sel(ALU_OP));
  Register #(.width(1)) u_CARRY_FLAG (.D(or_8_out), .en(or_5_out), .clk(CLK), .Q(CARRY_FLAG), .clr(or_9_out));
  or or_9 (or_9_out, decoder_5_out1, RESET);
  or or_10 (or_10_out, RESET, decoder_5_out3);
  or or_11 (or_11_out, ALU_NEGATIVE, decoder_5_out6);
  or or_12 (or_12_out, MICROCODE_STEP[21], decoder_5_out6);
  Register #(.width(1)) u_ZERO_FLAG (.D(or_6_out), .en(or_7_out), .clk(CLK), .Q(ZERO_FLAG), .clr(or_10_out));
  Register #(.width(1)) u_NEGATIVE_FLAG (.D(or_11_out), .en(or_12_out), .clk(CLK), .Q(NEGATIVE_FLAG), .clr(or_13_out));
  or or_13 (or_13_out, RESET, decoder_5_out5);
  Register #(.width(1)) INT_DIS_FLAG (
    .D(decoder_5_out8), .en(decoder_5_out8), .clk(CLK), .Q(INTERRUPT_DISABLE_FLAG), .clr(or_14_out));
  or or_14 (or_14_out, RESET, decoder_5_out7);
  Register #(.width(1)) DECIMAL_FALG (
    .D(decoder_5_out10), .en(decoder_5_out10), .clk(CLK), .Q(DECIMAL_FLAG), .clr(or_15_out));
  or or_15 (or_15_out, RESET, decoder_5_out9);
  Register #(.width(1)) u_OVERFLOW_FLAG (
    .D(decoder_5_out12), .en(decoder_5_out12), .clk(CLK), .Q(OVERFLOW_FLAG), .clr(or_16_out));
  or or_16 (or_16_out, RESET, decoder_5_out11);

  // Other names for the same wires on the sheet: WSOURCE[3:0] = MICROCODE_STEP[3:0];
  //   WDESTINATION[3:0] = MICROCODE_STEP[7:4];
  //   MICROCODE_STEP (some bits) = {ADDRESS_OFFSET_CI, ADDRESS_B, B_SEQ_RESET, COUNT_ADDRESS, CONSTV, FLAG_CMD, ALU_OP};
  //   UPDATE_CARRY = MICROCODE_STEP[17]; UPDATE_ZERO = MICROCODE_STEP[18]; UPDATE_NEGATIVE = MICROCODE_STEP[21];
  //   RESET_ADDRESS_OFFSET = MICROCODE_STEP[22]; SP_INCREMENT = MICROCODE_STEP[25]; SP_UPDATE = MICROCODE_STEP[26];
  //   SET_FLAG[3:0] = MICROCODE_STEP[30:27]

  // Notes on the sheet:
  //   contents of rom_1 (hex, n*v repeats v):
  //   5d 4c 800bf 500000 12*0 5d 4c 800bf 80eb 8007f 6b e1 80005f 180004f 4000af 98 24018e 500000 0 0 0 5d
  //   4c 800bf 500000 12*0 5d 4c 800bf 500000 12*0 5d 4c 800bf 500000 12*0 5d 4c 800bf 80098 100007f 6b
  //   8000af 24018e 500000 7*0 5d 4c 800bf 108007f 6b 80009f 26058e 500000 8*0 5d 4c 800bf 500000 12*0 5d
  //   4c 800bf 500000 12*0 5d 4c 800bf 80098 10000af 24018e 500000 9*0 5d 4c 800bf 98 26058e 500000 10*0
  //   5d 4c 800bf 500000 12*0 5d 4c 800bf 500000 12*0 5d 4c 800bf 80098 880eb 7f 100006f c000af 24018e
  //   500000 6*0 5d 4c 800bf 880eb 8007f 100006f c0009f 26058e 500000 7*0 5d 4c 800bf 500000 12*0 5d 4c
  //   800bf 5d 4c 80000 5000 9d af 3de 500000 5*0 5d 4c 800bf 80eb 8007f 6b c0005f 180004f e2 af 98 24018e
  //   500000 0 0 0 5d 4c 800bf 500000 12*0 5d 4c 800bf 500000 12*0 5d 4c 800bf 500000 12*0 5d 4c 800bf
  //   80098 100007f 6b e1 8000af 24018e 500000 6*0 5d 4c 800bf 108007f 6b e1 80009f 26058e 500000 7*0 5d
  //   4c 800bf 500000 12*0 5d 4c 800bf 8000000 500000 11*0 5d 4c 800bf 80098 880eb 7f 100006f e2 8000af
  //   24018e 500000 5*0 5d 4c 800bf 500000 12*0 5d 4c 800bf 500000 12*0 5d 4c 800bf 500000 12*0 5d 4c
  //   800bf 80098 880eb 7f 100006f e1 8000af 24018e 500000 5*0 5d 4c 800bf 880eb 8007f 100006f e1 80009f
  //   26058e 500000 6*0 5d 4c 800bf 500000 12*0 5d 4c 800bf 80000 80000 ac 9d 80eb df 10000cf 40806b
  //   6000073 8000fa 78000f9 500000 0 5d 4c 800bf 80eb 8007f 6b e1 80005f 180004f 4000af 98 24008e 500000
  //   0 0 0 5d 4c 800bf 500000 12*0 5d 4c 800bf 500000 12*0 5d 4c 800bf 500000 12*0 5d 4c 800bf 80098
  //   100007f 6b 8000af 24008e 500000 7*0 5d 4c 800bf 108007f 6b 80009f 26078e 500000 8*0 5d 4c 800bf
  //   500000 12*0 5d 4c 800bf 500000 12*0 5d 4c 800bf 80098 10000af 24008e 500000 9*0 5d 4c 800bf 98
  //   26078e 500000 10*0 5d 4c 800bf 500000 12*0 5d 4c 800bf 500000 12*0 5d 4c 800bf 80098 880eb 7f
  //   100006f c000af 24008e 500000 6*0 5d 4c 800bf 880eb 8007f 100006f c0009f 26078e 500000 7*0 5d 4c
  //   800bf 500000 12*0 5d 4c 800bf 5d 4c 80000 6000 9d af 3de 500000 5*0 5d 4c 800bf 80eb 8007f 6b c0005f
  //   180004f e2 af 98 24008e 500000 0 0 0 5d 4c 800bf 500000 12*0 5d 4c 800bf 500000 12*0 5d 4c 800bf
  //   500000 12*0 5d 4c 800bf 80098 100007f 6b e1 8000af 24008e 500000 6*0 5d 4c 800bf 108007f 6b e1
  //   80009f 26078e 500000 7*0 5d 4c 800bf 500000 12*0 5d 4c 800bf 10000000 500000 11*0 5d 4c 800bf 80098
  //   880eb 7f 100006f e2 8000af 24008e 500000 5*0 5d 4c 800bf 500000 12*0 5d 4c 800bf 500000 12*0 5d 4c
  //   800bf 500000 12*0 5d 4c 800bf 80098 880eb 7f 100006f e1 8000af 24008e 500000 5*0 5d 4c 800bf 880eb
  //   8007f 100006f e1 80009f 26078e 500000 6*0 5d 4c 800bf 500000 12*0 5d 4c 800bf 500000 12*0 5d 4c
  //   800bf 80eb 8007f 6b e1 80005f 180004f 4000af 98 24028e 500000 0 0 0 5d 4c 800bf 500000 12*0 5d 4c
  //   800bf 500000 12*0 5d 4c 800bf 500000 12*0 5d 4c 800bf 80098 100007f 6b 8000af 24028e 500000 7*0 5d
  //   4c 800bf 108007f 6b 80009f 26068e 500000 8*0 5d 4c 800bf 500000 12*0 5d 4c 800bf 806b 73 8000f8
  //   6000000 500000 8*0 5d 4c 800bf 80098 10000af 24028e 500000 9*0 5d 4c 800bf 98 26068e 500000 10*0 5d
  //   4c 800bf 500000 12*0 5d 4c 800bf 80eb df 10000cf 500000 9*0 5d 4c 800bf 80098 880eb 7f 100006f
  //   c000af 24028e 500000 6*0 5d 4c 800bf 880eb 8007f 100006f c0009f 26068e 500000 7*0 5d 4c 800bf 500000
  //   12*0 5d 4c 800bf 500000 12*0 5d 4c 800bf 80eb 8007f 6b c0005f 180004f e2 af 98 24028e 500000 0 0 0
  //   5d 4c 800bf 500000 12*0 5d 4c 800bf 500000 12*0 5d 4c 800bf 500000 12*0 5d 4c 800bf 80098 100007f 6b
  //   e1 8000af 24028e 500000 6*0 5d 4c 800bf 108007f 6b e1 80009f 26068e 500000 7*0 5d 4c 800bf 500000
  //   12*0 5d 4c 800bf 38000000 500000 11*0 5d 4c 800bf 80098 880eb 7f 100006f e2 8000af 24028e 500000 5*0
  //   5d 4c 800bf 500000 12*0 5d 4c 800bf 500000 12*0 5d 4c 800bf 500000 12*0 5d 4c 800bf 80098 880eb 7f
  //   100006f e1 8000af 24028e 500000 5*0 5d 4c 800bf 880eb 8007f 100006f e1 80009f 26068e 500000 6*0 5d
  //   4c 800bf 500000 12*0 5d 4c 800bf 4000000 4000000 40806b 73 8000cf 18000df 500000 6*0 5d 4c 800bf
  //   80eb 8007f 6b e1 80005f 180004f 4000af 98 26038e 500000 0 0 0 5d 4c 800bf 500000 12*0 5d 4c 800bf
  //   500000 12*0 5d 4c 800bf 500000 12*0 5d 4c 800bf 80098 100007f 6b 8000af 26038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
  //   000 No condition
  //   001 Carry clear
  //   010 Carry set
  //   011 Zero clear
  //   100 Zero set
  //   101 Negative clear
  //   110 Negative set
  //   (true when condition is not met)
  //   000 No change
  //   001 Carry clear
  //   010 Carry set
  //   011 Zero clear
  //   100 Zero set
  //   101 Negative clear
  //   110 Negative set
  //   1010 Decimal mode set
  //   1011 Overflow clear
  //   1100 Overflow set
  //   111 Interrupt disable clear
  //   1000 Interrupt disable set
  //   1001 Decimal mode clear
endmodule

module ASL (
  input  [7:0] D,
  output [7:0] Q,
  output CARRY
);


  assign CARRY = D[7];
  assign Q = {D[6:0], 1'b0};
endmodule

module LSR (
  input  [7:0] D,
  output CARRY,
  output [7:0] Q
);


  assign CARRY = D[0];
  assign Q = {1'b0, D[7:1]};
endmodule

module bROL (
  input  CIN,
  input  [7:0] D,
  output [7:0] Q,
  output CARRY
);


  assign CARRY = D[7];
  assign Q = {D[6:0], CIN};
endmodule

module bROR (
  input  [7:0] D,
  input  CIN,
  output CARRY,
  output [7:0] Q
);


  assign CARRY = D[0];
  assign Q = {CIN, D[7:1]};
endmodule
